# Fritzing sketch lorawan_freertos_arduino (saved by Fritzing 0.9.2b)
breadboards: 1

parts:
  Heltec_WiFi_LoRa_1 = Heltec WiFi LoRa 32 [part_number=HTIT-WB32LA]
  R2 = Resistor [tolerance=±5% resistance=470k package="2512 [SMD]"]
  R3 = Resistor [tolerance=±5% resistance=100k package="2512 [SMD]"]
  BAT1 = 18650 battery holder [package=battery-18650-kit]
  Part1 = BMP180 Breakout (GY-68)  # not connected

nets:
  N1: Heltec_WiFi_LoRa_1.pin_14, R2.Pin_0, R3.Pin_0
  N2: Heltec_WiFi_LoRa_1.pin_16, Heltec_WiFi_LoRa_1.pin_21
  N3: Heltec_WiFi_LoRa_1.pin_17, Heltec_WiFi_LoRa_1.pin_20
  N4: Heltec_WiFi_LoRa_1.pin_18, Heltec_WiFi_LoRa_1.pin_19, Heltec_WiFi_LoRa_1.pin_22, BAT1.-

notes:
  Cabo micro-USB --->
  - Programaçao
  - Carga da bateria
  - Alimentaçao via fonte chaveada 5V/2A

custom parts:
  Heltec WiFi LoRa 32: Heltec WiFi LoRa 32 WiFi LoRa 32 is a classic IoT dev-board designed & produced by Heltec Automation(TM). It’s a highly integrated product based on ESP32 + SX127x, it has Wi-Fi, BLE, LoRa functions, also Li-Po battery management system, 0.96″ OLED are also included. It’s the best choice for smart cities, smart farms, smart home, and IoT makers.
  18650 battery holder: 18650 Battery Holder
  BMP180 Breakout (GY-68): This is a simple breakout board for the BMP180, a high-precision, low-power barometric pressure sensor made by Bosch Sensortec. The range of measurement is from 300hPa to 1100hPa. The sensor can be supplied with voltage ranging from 1.8V to 3.6V. Operating temperature range is -40 to +85 °C. This particular breakout board (or perhaps the configuration) is produced by Shenzhen Keep Power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
